# Fritzing sketch lab03 (saved by Fritzing 0.9.3b)
breadboards: 1

parts:
  U1 = ESP32-38PinWide [part_number=ESP32-38PinWide]
  A1 = BBAA100043
  R1 = Resistor [tolerance=±5% resistance=220 package="2010 [SMD]"]
  R2 = Resistor [tolerance=±5% resistance=220 package="2010 [SMD]"]
  R3 = Resistor [tolerance=±5% resistance=220 package="2010 [SMD]"]

nets:
  N1: U1.GND, A1.pin4
  N2: U1.GPIO16, R1.Pin_0
  N3: U1.GPIO17, R2.Pin_0
  N4: U1.GPIO5, R3.Pin_0
  N5: A1.pin1, R1.Pin_1
  N6: A1.pin2, R2.Pin_1
  N7: A1.pin3, R3.Pin_1

notes:
  R = 330 Ohm
  GND >>> GND
  GPIO5 >>> red
  GPIO17 >>> yellow
  GPIO16 >>> green

custom parts:
  ESP32-38PinWide: Generic 38-Pin ESP32 with wide format (only access to one side of pins on a breadboard) based on Stephen Lilley's HiLetgo ESP-WROOM-32 ESP32 ESP-32S Development Board.
  BBAA100043: BBAA100043 traffic light module.
