# Fritzing sketch lab06_ADCsoilMC (saved by Fritzing 0.9.3b)
breadboards: 1

parts:
  U1 = ESP32-38PinWide [part_number=ESP32-38PinWide]
  A1 = BBAA100043
  R1 = Resistor [tolerance=±5% resistance=220 package="2010 [SMD]"]
  R2 = Resistor [tolerance=±5% resistance=220 package="2010 [SMD]"]
  R3 = Resistor [tolerance=±5% resistance=220 package="2010 [SMD]"]
  S1 = Pushbutton [package="[THT]"]
  S2 = Pushbutton [package="[THT]"]
  S3 = Pushbutton [package="[THT]"]
  R4 = Resistor [tolerance=±5% resistance=220 package=THT]
  R5 = Resistor [tolerance=±5% resistance=220 package=THT]
  R6 = Resistor [tolerance=±5% resistance=220 package=THT]
  R7 = Rotary Potentiometer (Large) [maximum_resistance=100kΩ package=THT]
  Capacitive_Soil_Moisture_Sensor1 = DFRobot Capacitive Soil Moisture Sensor V1.0 [part_number=SEN0193]

nets:
  N1: U1.3.3, S1.Pin_1, S1.Pin_2, S2.Pin_1, S2.Pin_2, S3.Pin_1, S3.Pin_2, R7.leg2, Capacitive_Soil_Moisture_Sensor1.VCC
  N2: U1.GPIO34, S1.Pin_3, S1.Pin_4, R4.Pin_1
  N3: U1.GPIO35, Capacitive_Soil_Moisture_Sensor1.A
  GND: U1.GND, A1.pin4, R4.Pin_0, R5.Pin_0, R6.Pin_0, R7.leg1, Capacitive_Soil_Moisture_Sensor1.GND
  N4: U1.GPIO4, R7.wiper
  N5: U1.GPIO16, R1.Pin_0
  N6: U1.GPIO17, R2.Pin_0
  N7: U1.GPIO5, R3.Pin_0
  N8: A1.pin1, R1.Pin_1
  N9: A1.pin2, R2.Pin_1
  N10: A1.pin3, R3.Pin_1
  N11: S2.Pin_3, S2.Pin_4, R5.Pin_1
  N12: S3.Pin_3, S3.Pin_4, R6.Pin_1

notes:
  R = 330 Ohm
  GND >>> GND
  GPIO5 >>> red
  GPIO17 >>> yellow
  GPIO16 >>> green
  R = 330 Ohm resistor
  GPI34 >>> Button_01
  GPI35 >>> Button_02
  GPI32 >>> Button_03
  GPIO4 >>> Pot
  GPI35 >>> Soil Sensor

custom parts:
  ESP32-38PinWide: Generic 38-Pin ESP32 with wide format (only access to one side of pins on a breadboard) based on Stephen Lilley's HiLetgo ESP-WROOM-32 ESP32 ESP-32S Development Board.
  BBAA100043: BBAA100043 traffic light module.
  DFRobot Capacitive Soil Moisture Sensor V1.0: DFRobot Capacitive Soil Moisture Sensor V1.0 This product measures soil moisture levels by capacitive sensing, rather than resistive sensing like other types of moisture sensor. It is made of a corrosion resistant material giving it a long service life. Insert it into soil and impress your friends with the real-time soil moisture data! The product includes an on-board voltage regulator which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
