# Fritzing sketch lab17_DHT22 (saved by Fritzing 0.9.3b)
breadboards: 1

parts:
  U1 = ESP32-38PinWide [part_number=ESP32-38PinWide]
  Capacitive_Soil_Moisture_Sensor1 = DFRobot Capacitive Soil Moisture Sensor V1.0 [part_number=SEN0193]
  DHT1 = DHT22 Humidity and Temperature Sensor
  R1 = Resistor [tolerance=±5% resistance=220 package=THT]

nets:
  VCC: U1.3.3, Capacitive_Soil_Moisture_Sensor1.VCC, DHT1.VDD, R1.Pin_0
  N1: U1.GPIO35, Capacitive_Soil_Moisture_Sensor1.A
  N2: U1.GPIO14, DHT1.DATA, R1.Pin_1
  GND: U1.GND, Capacitive_Soil_Moisture_Sensor1.GND, DHT1.GND

notes:
  R = 10 kOhm
  #DHT22
  Pin1 >>> 3v3
  Pin2 >>> GPIO14
  Pin3 >>> -
  Pin4 >>> GND
  #Soil Sensor
  Pin1 >>> GPI35
  Pin2 >>> 3v3
  Pin3 >>> GND

custom parts:
  ESP32-38PinWide: Generic 38-Pin ESP32 with wide format (only access to one side of pins on a breadboard) based on Stephen Lilley's HiLetgo ESP-WROOM-32 ESP32 ESP-32S Development Board.
  DFRobot Capacitive Soil Moisture Sensor V1.0: DFRobot Capacitive Soil Moisture Sensor V1.0 This product measures soil moisture levels by capacitive sensing, rather than resistive sensing like other types of moisture sensor. It is made of a corrosion resistant material giving it a long service life. Insert it into soil and impress your friends with the real-time soil moisture data! The product includes an on-board voltage regulator which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
