# Fritzing sketch lab22_ds18b20_multi (saved by Fritzing 0.9.3b)
breadboards: 1

parts:
  U1 = ESP32-38PinWide [part_number=ESP32-38PinWide]
  Squix1 = OLED 0.96" 128x64 I2C SSD1306
  DS2 = DS18B20 1-Wire Temperature Sensor Probe
  R1 = Resistor [tolerance=±5% resistance=220 package=THT]
  DS3 = DS18B20 1-Wire Temperature Sensor Probe
  R3 = Resistor [tolerance=±5% resistance=220 package=THT]  # not connected
  R4 = Resistor [tolerance=±5% resistance=220 package=THT]  # not connected
  DS4 = DS18B20 1-Wire Temperature Sensor Probe

nets:
  VDD: U1.3.3, Squix1.VCC, DS2.VDD, R1.Pin_0, DS3.VDD, DS4.VDD
  GND: U1.GND, Squix1.GND, DS2.GND, DS3.GND, DS4.GND
  N1: U1.GPIO4, DS2.DQ, R1.Pin_1, DS3.DQ, DS4.DQ
  N2: U1.GPIO21, Squix1.SCA
  N3: U1.GPIO22, Squix1.SCL

notes:
  #DS18B20 Temperature Sensor
  Pin1 >>> GND
  Pin2 >>> GPIO4
  Pin3 >>> 3v3

custom parts:
  ESP32-38PinWide: Generic 38-Pin ESP32 with wide format (only access to one side of pins on a breadboard) based on Stephen Lilley's HiLetgo ESP-WROOM-32 ESP32 ESP-32S Development Board.
